// Digital circuit ALU.dig as structural Verilog
module ALU (
  input  [15:0] A,
  input  [15:0] B,
  input  [3:0] Opcode,
  input  clk,
  output [15:0] Out,
  output out_6
);

  wire U1_B_0, U2_B_0, U2_C_0, U3_C_0;
  wire [1:1] U1_d, U3_d;
  wire [3:2] U2_d;

  EEPROM #(.AddrBits(17), .Bits(8)) U1 (
    .A({Opcode, A[15:10], B[15:10], U2_C_0}), .CS(1'b1), .WE(1'b0), .OE(1'b1),
    .D({Out[15:10], U1_d[1], U1_B_0}));
  EEPROM #(.AddrBits(17), .Bits(8)) U2 (
    .A({Opcode, A[9:6], B[9:6], 3'b000, U1_B_0, U3_C_0}), .CS(1'b1), .WE(1'b0), .OE(1'b1),
    .D({Out[9:6], U2_d, U2_B_0, U2_C_0}));
  EEPROM #(.AddrBits(17), .Bits(8)) U3 (
    .A({Opcode, A[5:0], B[5:0], U2_B_0}), .CS(1'b1), .WE(1'b0), .OE(1'b1), .D({Out[5:0], U3_d[1], U3_C_0}));

  assign out_6 = clk;

  // Notes on the sheet:
  //   contents of U1 (hex, n*v repeats v):
  //   128*0,128*4,128*8,128*c,128*10,128*14,128*18,128*1c,128*20,128*24
  //   ,128*28,128*2c,128*30,128*34,128*38,128*3c,128*40,128*44,128*48
  //   ,128*4c,128*50,128*54,128*58,128*5c,128*60,128*64,128*68,128*6c
  //   ,128*70,128*74,128*78,128*7c,128*80,128*84,128*88,128*8c,128*90
  //   ,128*94,128*98,128*9c,128*a0,128*a4,128*a8,128*ac,128*b0,128*b4
  //   ,128*b8,128*bc,128*c0,128*c4,128*c8,128*cc,128*d0,128*d4,128*d8
  //   ,128*dc,128*e0,128*e4,128*e8,128*ec,128*f0,128*f4,128*f8,128*fc
  //   ,128*0,128*4,128*8,128*c,128*10,128*14,128*18,128*1c,128*20,128*24
  //   ,128*28,128*2c,128*30,128*34,128*38,128*3c,128*40,128*44,128*48
  //   ,128*4c,128*50,128*54,128*58,128*5c,128*60,128*64,128*68,128*6c
  //   ,128*70,128*74,128*78,128*7c,128*80,128*84,128*88,128*8c,128*90
  //   ,128*94,128*98,128*9c,128*a0,128*a4,128*a8,128*ac,128*b0,128*b4
  //   ,128*b8,128*bc,128*c0,128*c4,128*c8,128*cc,128*d0,128*d4,128*d8
  //   ,128*dc,128*e0,128*e4,128*e8,128*ec,128*f0,128*f4,128*f8,128*fc
  //   ,128*0,128*4,128*8,128*c,128*10,128*14,128*18,128*1c,128*20,128*24
  //   ,128*28,128*2c,128*30,128*34,128*38,128*3c,128*40,128*44,128*48
  //   ,128*4c,128*50,128*54,128*58,128*5c,128*60,128*64,128*68,128*6c
  //   ,128*70,128*74,128*78,128*7c,128*80,128*84,128*88,128*8c,128*90
  //   ,128*94,128*98,128*9c,128*a0,128*a4,128*a8,128*ac,128*b0,128*b4
  //   ,128*b8,128*bc,128*c0,128*c4,128*c8,128*cc,128*d0,128*d4,128*d8
  //   ,128*dc,128*e0,128*e4,128*e8,128*ec,128*f0,128*f4,128*f8,128*fc
  //   ,128*0,128*4,128*8,128*c,128*10,128*14,128*18,128*1c,128*20,128*24
  //   ,128*28,128*2c,128*30,128*34,128*38,128*3c,128*40,128*44,128*48
  //   ,128*4c,128*50,128*54,128*58,128*5c,128*60,128*64,128*68,128*6c
  //   ,128*70,128*74,128*78,128*7c,128*80,128*84,128*88,128*8c,128*90
  //   ,128*94,128*98,128*9c,128*a0,128*a4,128*a8,128*ac,128*b0,128*b4
  //   ,128*b8,128*bc,128*c0,128*c4,128*c8,128*cc,128*d0,128*d4,128*d8
  //   ,128*dc,128*e0,128*e4,128*e8,128*ec,128*f0,128*f4,128*f8,128*fc
  //   ,0,0,4,4,8,8,c,c,10,10,14,14,18,18,1c,1c,20,20,24,24,28,28,2c,2c
  //   ,30,30,34,34,38,38,3c,3c,40,40,44,44,48,48,4c,4c,50,50,54,54,58,58
  //   ,5c,5c,60,60,64,64,68,68,6c,6c,70,70,74,74,78,78,7c,7c,80,80,84,84
  //   ,88,88,8c,8c,90,90,94,94,98,98,9c,9c,a0,a0,a4,a4,a8,a8,ac,ac,b0,b0
  //   ,b4,b4,b8,b8,bc,bc,c0,c0,c4,c4,c8,c8,cc,cc,d0,d0,d4,d4,d8,d8,dc,dc
  //   ,e0,e0,e4,e4,e8,e8,ec,ec,f0,f0,f4,f4,f8,f8,fc,fc,4*4,4*c,4*14
  //   ,4*1c,4*24,4*2c,4*34,4*3c,4*44,4*4c,4*54,4*5c,4*64,4*6c,4*74,4*7c
  //   ,4*84,4*8c,4*94,4*9c,4*a4,4*ac,4*b4,4*bc,4*c4,4*cc,4*d4,4*dc,4*e4
  //   ,4*ec,4*f4,4*fc,8,8,c,c,8,8,c,c,18,18,1c,1c,18,18,1c,1c,28,28
  //   ,2c,2c,28,28,2c,2c,38,38,3c,3c,38,38,3c,3c,48,48,4c,4c,48,48,4c,4c
  //   ,58,58,5c,5c,58,58,5c,5c,68,68,6c,6c,68,68,6c,6c,78,78,7c,7c,78,78
  //   ,7c,7c,88,88,8c,8c,88,88,8c,8c,98,98,9c,9c,98,98,9c,9c,a8,a8,ac,ac
  //   ,a8,a8,ac,ac,b8,b8,bc,bc,b8,b8,bc,bc,c8,c8,cc,cc,c8,c8,cc,cc,d8,d8
  //   ,dc,dc,d8,d8,dc,dc,e8,e8,ec,ec,e8,e8,ec,ec,f8,f8,fc,fc,f8,f8,fc,fc
  //   ,8*c,8*1c,8*2c,8*3c,8*4c,8*5c,8*6c,8*7c,8*8c,8*9c,8*ac,8*bc,8*cc
  //   ,8*dc,8*ec,8*fc,10,10,14,14,18,18,1c,1c,10,10,14,14,18,18,1c,1c
  //   ,30,30,34,34,38,38,3c,3c,30,30,34,34,38,38,3c,3c,50,50,54,54,58,58
  //   ,5c,5c,50,50,54,54,58,58,5c,5c,70,70,74,74,78,78,7c,7c,70,70,74,74
  //   ,78,78,7c,7c,90,90,94,94,98,98,9c,9c,90,90,94,94,98,98,9c,9c,b0,b0
  //   ,b4,b4,b8,b8,bc,bc,b0,b0,b4,b4,b8,b8,bc,bc,d0,d0,d4,d4,d8,d8,dc,dc
  //   ,d0,d0,d4,d4,d8,d8,dc,dc,f0,f0,f4,f4,f8,f8,fc,fc,f0,f0,f4,f4,f8,f8
  //   ,fc,fc,4*14,4*1c,4*14,4*1c,4*34,4*3c,4*34,4*3c,4*54,4*5c,4*54
  //   ,4*5c,4*74,4*7c,4*74,4*7c,4*94,4*9c,4*94,4*9c,4*b4,4*bc,4*b4,4*bc
  //   ,4*d4,4*dc,4*d4,4*dc,4*f4,4*fc,4*f4,4*fc,18,18,1c,1c,18,18,1c,1c
  //   ,18,18,1c,1c,18,18,1c,1c,38,38,3c,3c,38,38,3c,3c,38,38,3c,3c,38,38
  //   ,3c,3c,58,58,5c,5c,58,58,5c,5c,58,58,5c,5c,58,58,5c,5c,78,78,7c,7c
  //   ,78,78,7c,7c,78,78,7c,7c,78,78,7c,7c,98,98,9c,9c,98,98,9c,9c,98,98
  //   ,9c,9c,98,98,9c,9c,b8,b8,bc,bc,b8,b8,bc,bc,b8,b8,bc,bc,b8,b8,bc,bc
  //   ,d8,d8,dc,dc,d8,d8,dc,dc,d8,d8,dc,dc,d8,d8,dc,dc,f8,f8,fc,fc,f8,f8
  //   ,fc,fc,f8,f8,fc,fc,f8,f8,fc,fc,16*1c,16*3c,16*5c,16*7c,16*9c,16*bc
  //   ,16*dc,16*fc,20,20,24,24,28,28,2c,2c,30,30,34,34,38,38,3c,3c,20,20
  //   ,24,24,28,28,2c,2c,30,30,34,34,38,38,3c,3c,60,60,64,64,68,68,6c,6c
  //   ,70,70,74,74,78,78,7c,7c,60,60,64,64,68,68,6c,6c,70,70,74,74,78,78
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  //   contents of U2 (hex, n*v repeats v):
  //   512*0,512*10,512*20,512*30,512*40,512*50,512*60,512*70,512*80
  //   ,512*90,512*a0,512*b0,512*c0,512*d0,512*e0,512*f0,512*0,512*10
  //   ,512*20,512*30,512*40,512*50,512*60,512*70,512*80,512*90,512*a0
  //   ,512*b0,512*c0,512*d0,512*e0,512*f0,512*0,512*10,512*20,512*30
  //   ,512*40,512*50,512*60,512*70,512*80,512*90,512*a0,512*b0,512*c0
  //   ,512*d0,512*e0,512*f0,512*0,512*10,512*20,512*30,512*40,512*50
  //   ,512*60,512*70,512*80,512*90,512*a0,512*b0,512*c0,512*d0,512*e0
  //   ,512*f0,32*0,32*10,32*20,32*30,32*40,32*50,32*60,32*70,32*80,32*90
  //   ,32*a0,32*b0,32*c0,32*d0,32*e0,32*f0,64*10,64*30,64*50,64*70,64*90
  //   ,64*b0,64*d0,64*f0,32*20,32*30,32*20,32*30,32*60,32*70,32*60,32*70
  //   ,32*a0,32*b0,32*a0,32*b0,32*e0,32*f0,32*e0,32*f0,128*30,128*70
  //   ,128*b0,128*f0,32*40,32*50,32*60,32*70,32*40,32*50,32*60,32*70
  //   ,32*c0,32*d0,32*e0,32*f0,32*c0,32*d0,32*e0,32*f0,64*50,64*70,64*50
  //   ,64*70,64*d0,64*f0,64*d0,64*f0,32*60,32*70,32*60,32*70,32*60,32*70
  //   ,32*60,32*70,32*e0,32*f0,32*e0,32*f0,32*e0,32*f0,32*e0,32*f0,256*70
  //   ,256*f0,32*80,32*90,32*a0,32*b0,32*c0,32*d0,32*e0,32*f0,32*80
  //   ,32*90,32*a0,32*b0,32*c0,32*d0,32*e0,32*f0,64*90,64*b0,64*d0,64*f0
  //   ,64*90,64*b0,64*d0,64*f0,32*a0,32*b0,32*a0,32*b0,32*e0,32*f0,32*e0
  //   ,32*f0,32*a0,32*b0,32*a0,32*b0,32*e0,32*f0,32*e0,32*f0,128*b0
  //   ,128*f0,128*b0,128*f0,32*c0,32*d0,32*e0,32*f0,32*c0,32*d0,32*e0
  //   ,32*f0,32*c0,32*d0,32*e0,32*f0,32*c0,32*d0,32*e0,32*f0,64*d0,64*f0
  //   ,64*d0,64*f0,64*d0,64*f0,64*d0,64*f0,32*e0,32*f0,32*e0,32*f0,32*e0
  //   ,32*f0,32*e0,32*f0,32*e0,32*f0,32*e0,32*f0,32*e0,32*f0,32*e0,1056*f0
  //   ,512*e0,512*d0,512*c0,512*b0,512*a0,512*90,512*80,512*70,512*60
  //   ,512*50,512*40,512*30,512*20,512*10,1056*0,32*10,32*0,32*10,32*0
  //   ,32*10,32*0,32*10,32*0,32*10,32*0,32*10,32*0,32*10,32*0,32*10
  //   ,64*0,64*20,64*0,64*20,64*0,64*20,64*0,64*20,32*0,32*10,32*20
  //   ,32*30,32*0,32*10,32*20,32*30,32*0,32*10,32*20,32*30,32*0,32*10
  //   ,32*20,32*30,128*0,128*40,128*0,128*40,32*0,32*10,32*0,32*10,32*40
  //   ,32*50,32*40,32*50,32*0,32*10,32*0,32*10,32*40,32*50,32*40,32*50
  //   ,64*0,64*20,64*40,64*60,64*0,64*20,64*40,64*60,32*0,32*10,32*20
  //   ,32*30,32*40,32*50,32*60,32*70,32*0,32*10,32*20,32*30,32*40,32*50
  //   ,32*60,32*70,256*0,256*80,32*0,32*10,32*0,32*10,32*0,32*10,32*0
  //   ,32*10,32*80,32*90,32*80,32*90,32*80,32*90,32*80,32*90,64*0,64*20
  //   ,64*0,64*20,64*80,64*a0,64*80,64*a0,32*0,32*10,32*20,32*30,32*0
  //   ,32*10,32*20,32*30,32*80,32*90,32*a0,32*b0,32*80,32*90,32*a0,32*b0
  //   ,128*0,128*40,128*80,128*c0,32*0,32*10,32*0,32*10,32*40,32*50
  //   ,32*40,32*50,32*80,32*90,32*80,32*90,32*c0,32*d0,32*c0,32*d0,64*0
  //   ,64*20,64*40,64*60,64*80,64*a0,64*c0,64*e0,32*0,32*10,32*20,32*30
  //   ,32*40,32*50,32*60,32*70,32*80,32*90,32*a0,32*b0,32*c0,32*d0,32*e0
  //   ,32*f0,32*0,32*10,32*20,32*30,32*40,32*50,32*60,32*70,32*80,32*90
  //   ,32*a0,32*b0,32*c0,32*d0,32*e0,32*f0,32*10,32*0,32*30,32*20,32*50
  //   ,32*40,32*70,32*60,32*90,32*80,32*b0,32*a0,32*d0,32*c0,32*f0,32*e0
  //   ,32*20,32*30,32*0,32*10,32*60,32*70,32*40,32*50,32*a0,32*b0,32*80
  //   ,32*90,32*e0,32*f0,32*c0,32*d0,32*30,32*20,32*10,32*0,32*70,32*60
  //   ,32*50,32*40,32*b0,32*a0,32*90,32*80,32*f0,32*e0,32*d0,32*c0,32*40
  //   ,32*50,32*60,32*70,32*0,32*10,32*20,32*30,32*c0,32*d0,32*e0,32*f0
  //   ,32*80,32*90,32*a0,32*b0,32*50,32*40,32*70,32*60,32*10,32*0,32*30
  //   ,32*20,32*d0,32*c0,32*f0,32*e0,32*90,32*80,32*b0,32*a0,32*60,32*70
  //   ,32*40,32*50,32*20,32*30,32*0,32*10,32*e0,32*f0,32*c0,32*d0,32*a0
  //   ,32*b0,32*80,32*90,32*70,32*60,32*50,32*40,32*30,32*20,32*10,32*0
  //   ,32*f0,32*e0,32*d0,32*c0,32*b0,32*a0,32*90,64*80,32*90,32*a0,32*b0
  //   ,32*c0,32*d0,32*e0,32*f0,32*0,32*10,32*20,32*30,32*40,32*50,32*60
  //   ,32*70,32*90,32*80,32*b0,32*a0,32*d0,32*c0,32*f0,32*e0,32*10,32*0
  //   ,32*30,32*20,32*50,32*40,32*70,32*60,32*a0,32*b0,32*80,32*90,32*e0
  //   ,32*f0,32*c0,32*d0,32*20,32*30,32*0,32*10,32*60,32*70,32*40,32*50
  //   ,32*b0,32*a0,32*90,32*80,32*f0,32*e0,32*d0,32*c0,32*30,32*20,32*10
  //   ,32*0,32*70,32*60,32*50,32*40,32*c0,32*d0,32*e0,32*f0,32*80,32*90
  //   ,32*a0,32*b0,32*40,32*50,32*60,32*70,32*0,32*10,32*20,32*30,32*d0
  //   ,32*c0,32*f0,32*e0,32*90,32*80,32*b0,32*a0,32*50,32*40,32*70,32*60
  //   ,32*10,32*0,32*30,32*20,32*e0,32*f0,32*c0,32*d0,32*a0,32*b0,32*80
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  //   contents of U3 (hex, n*v repeats v):
  //   128*0,128*4,128*8,128*c,128*10,128*14,128*18,128*1c,128*20,128*24
  //   ,128*28,128*2c,128*30,128*34,128*38,128*3c,128*40,128*44,128*48
  //   ,128*4c,128*50,128*54,128*58,128*5c,128*60,128*64,128*68,128*6c
  //   ,128*70,128*74,128*78,128*7c,128*80,128*84,128*88,128*8c,128*90
  //   ,128*94,128*98,128*9c,128*a0,128*a4,128*a8,128*ac,128*b0,128*b4
  //   ,128*b8,128*bc,128*c0,128*c4,128*c8,128*cc,128*d0,128*d4,128*d8
  //   ,128*dc,128*e0,128*e4,128*e8,128*ec,128*f0,128*f4,128*f8,128*fc
  //   ,128*0,128*4,128*8,128*c,128*10,128*14,128*18,128*1c,128*20,128*24
  //   ,128*28,128*2c,128*30,128*34,128*38,128*3c,128*40,128*44,128*48
  //   ,128*4c,128*50,128*54,128*58,128*5c,128*60,128*64,128*68,128*6c
  //   ,128*70,128*74,128*78,128*7c,128*80,128*84,128*88,128*8c,128*90
  //   ,128*94,128*98,128*9c,128*a0,128*a4,128*a8,128*ac,128*b0,128*b4
  //   ,128*b8,128*bc,128*c0,128*c4,128*c8,128*cc,128*d0,128*d4,128*d8
  //   ,128*dc,128*e0,128*e4,128*e8,128*ec,128*f0,128*f4,128*f8,128*fc
  //   ,128*0,128*4,128*8,128*c,128*10,128*14,128*18,128*1c,128*20,128*24
  //   ,128*28,128*2c,128*30,128*34,128*38,128*3c,128*40,128*44,128*48
  //   ,128*4c,128*50,128*54,128*58,128*5c,128*60,128*64,128*68,128*6c
  //   ,128*70,128*74,128*78,128*7c,128*80,128*84,128*88,128*8c,128*90
  //   ,128*94,128*98,128*9c,128*a0,128*a4,128*a8,128*ac,128*b0,128*b4
  //   ,128*b8,128*bc,128*c0,128*c4,128*c8,128*cc,128*d0,128*d4,128*d8
  //   ,128*dc,128*e0,128*e4,128*e8,128*ec,128*f0,128*f4,128*f8,128*fc
  //   ,128*0,128*4,128*8,128*c,128*10,128*14,128*18,128*1c,128*20,128*24
  //   ,128*28,128*2c,128*30,128*34,128*38,128*3c,128*40,128*44,128*48
  //   ,128*4c,128*50,128*54,128*58,128*5c,128*60,128*64,128*68,128*6c
  //   ,128*70,128*74,128*78,128*7c,128*80,128*84,128*88,128*8c,128*90
  //   ,128*94,128*98,128*9c,128*a0,128*a4,128*a8,128*ac,128*b0,128*b4
  //   ,128*b8,128*bc,128*c0,128*c4,128*c8,128*cc,128*d0,128*d4,128*d8
  //   ,128*dc,128*e0,128*e4,128*e8,128*ec,128*f0,128*f4,128*f8,128*fc
  //   ,0,0,4,4,8,8,c,c,10,10,14,14,18,18,1c,1c,20,20,24,24,28,28,2c,2c
  //   ,30,30,34,34,38,38,3c,3c,40,40,44,44,48,48,4c,4c,50,50,54,54,58,58
  //   ,5c,5c,60,60,64,64,68,68,6c,6c,70,70,74,74,78,78,7c,7c,80,80,84,84
  //   ,88,88,8c,8c,90,90,94,94,98,98,9c,9c,a0,a0,a4,a4,a8,a8,ac,ac,b0,b0
  //   ,b4,b4,b8,b8,bc,bc,c0,c0,c4,c4,c8,c8,cc,cc,d0,d0,d4,d4,d8,d8,dc,dc
  //   ,e0,e0,e4,e4,e8,e8,ec,ec,f0,f0,f4,f4,f8,f8,fc,fc,4*4,4*c,4*14
  //   ,4*1c,4*24,4*2c,4*34,4*3c,4*44,4*4c,4*54,4*5c,4*64,4*6c,4*74,4*7c
  //   ,4*84,4*8c,4*94,4*9c,4*a4,4*ac,4*b4,4*bc,4*c4,4*cc,4*d4,4*dc,4*e4
  //   ,4*ec,4*f4,4*fc,8,8,c,c,8,8,c,c,18,18,1c,1c,18,18,1c,1c,28,28
  //   ,2c,2c,28,28,2c,2c,38,38,3c,3c,38,38,3c,3c,48,48,4c,4c,48,48,4c,4c
  //   ,58,58,5c,5c,58,58,5c,5c,68,68,6c,6c,68,68,6c,6c,78,78,7c,7c,78,78
  //   ,7c,7c,88,88,8c,8c,88,88,8c,8c,98,98,9c,9c,98,98,9c,9c,a8,a8,ac,ac
  //   ,a8,a8,ac,ac,b8,b8,bc,bc,b8,b8,bc,bc,c8,c8,cc,cc,c8,c8,cc,cc,d8,d8
  //   ,dc,dc,d8,d8,dc,dc,e8,e8,ec,ec,e8,e8,ec,ec,f8,f8,fc,fc,f8,f8,fc,fc
  //   ,8*c,8*1c,8*2c,8*3c,8*4c,8*5c,8*6c,8*7c,8*8c,8*9c,8*ac,8*bc,8*cc
  //   ,8*dc,8*ec,8*fc,10,10,14,14,18,18,1c,1c,10,10,14,14,18,18,1c,1c
  //   ,30,30,34,34,38,38,3c,3c,30,30,34,34,38,38,3c,3c,50,50,54,54,58,58
  //   ,5c,5c,50,50,54,54,58,58,5c,5c,70,70,74,74,78,78,7c,7c,70,70,74,74
  //   ,78,78,7c,7c,90,90,94,94,98,98,9c,9c,90,90,94,94,98,98,9c,9c,b0,b0
  //   ,b4,b4,b8,b8,bc,bc,b0,b0,b4,b4,b8,b8,bc,bc,d0,d0,d4,d4,d8,d8,dc,dc
  //   ,d0,d0,d4,d4,d8,d8,dc,dc,f0,f0,f4,f4,f8,f8,fc,fc,f0,f0,f4,f4,f8,f8
  //   ,fc,fc,4*14,4*1c,4*14,4*1c,4*34,4*3c,4*34,4*3c,4*54,4*5c,4*54
  //   ,4*5c,4*74,4*7c,4*74,4*7c,4*94,4*9c,4*94,4*9c,4*b4,4*bc,4*b4,4*bc
  //   ,4*d4,4*dc,4*d4,4*dc,4*f4,4*fc,4*f4,4*fc,18,18,1c,1c,18,18,1c,1c
  //   ,18,18,1c,1c,18,18,1c,1c,38,38,3c,3c,38,38,3c,3c,38,38,3c,3c,38,38
  //   ,3c,3c,58,58,5c,5c,58,58,5c,5c,58,58,5c,5c,58,58,5c,5c,78,78,7c,7c
  //   ,78,78,7c,7c,78,78,7c,7c,78,78,7c,7c,98,98,9c,9c,98,98,9c,9c,98,98
  //   ,9c,9c,98,98,9c,9c,b8,b8,bc,bc,b8,b8,bc,bc,b8,b8,bc,bc,b8,b8,bc,bc
  //   ,d8,d8,dc,dc,d8,d8,dc,dc,d8,d8,dc,dc,d8,d8,dc,dc,f8,f8,fc,fc,f8,f8
  //   ,fc,fc,f8,f8,fc,fc,f8,f8,fc,fc,16*1c,16*3c,16*5c,16*7c,16*9c,16*bc
  //   ,16*dc,16*fc,20,20,24,24,28,28,2c,2c,30,30,34,34,38,38,3c,3c,20,20
  //   ,24,24,28,28,2c,2c,30,30,34,34,38,38,3c,3c,60,60,64,64,68,68,6c,6c
  //   ,70,70,74,74,78,78,7c,7c,60,60,64,64,68,68,6c,6c,70,70,74,74,78,78
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endmodule
