// Digital circuit RGBMatrix.dig as structural Verilog
module RGBMatrix (
  input  [11:0] Addr,
  input  [15:0] Data,
  input  clk,
  output R1,
  output R2,
  output G1,
  output G2,
  output B1,
  output B2,
  output LAT,
  output OE,
  output A,
  output B,
  output C,
  output D,
  output CLK3,
  output CLK4
);

  wire dipswitch_1_out, STRHI, STRLO;
  wire [0:0] counter_1_out_2;
  wire [2:0] ramdualaccess_1_d2_2, ramdualaccess_3_d2_2;
  wire [4:0] ramdualaccess_1_d2, ramdualaccess_3_d2;
  wire [6:0] ramdualaccess_2_d2, ramdualaccess_4_d2;
  wire [7:2] eeprom_1_d, eeprom_2_d, eeprom_3_d;
  wire [7:7] ramdualaccess_2_d2_2, ramdualaccess_4_d2_2;
  wire [11:0] counter_1_out;

  Counter #(.Bits(12)) counter_1 (
    .en(1'b1), .C(clk), .clr(dipswitch_1_out),
    .out({counter_1_out[11], A, B, C, D, counter_1_out_2[0], counter_1_out[5:0]}));  // open: ovf
  DipSwitch dipswitch_1 (.out(dipswitch_1_out));
  Demultiplexer demultiplexer_1 (.sel(Addr[10]), .in(Data[15]), .out_0(STRLO), .out_1(STRHI));
  and and_1 (LAT, counter_1_out[0], counter_1_out[1], counter_1_out[2], counter_1_out[3], counter_1_out[4], counter_1_out[5]);
  RAMDualAccess #(.AddrBits(11), .Bits(8)) ramdualaccess_1 (
    .str(STRLO), .C(clk), .ld(1'b1), .A1({Addr[9:0], Addr[11]}), .Din1(Data[7:0]),
    .A2({counter_1_out[11], B, C, D, counter_1_out_2[0], counter_1_out[5:0]}),
    .D2({ramdualaccess_1_d2_2, ramdualaccess_1_d2}));  // open: D1
  RAMDualAccess #(.AddrBits(11), .Bits(8)) ramdualaccess_2 (
    .str(STRLO), .C(clk), .ld(1'b1), .A1({Addr[9:0], Addr[11]}), .Din1({1'b0, Data[14:8]}),
    .A2({counter_1_out[11], B, C, D, counter_1_out_2[0], counter_1_out[5:0]}),
    .D2({ramdualaccess_2_d2_2[7], ramdualaccess_2_d2}));  // open: D1
  RAMDualAccess #(.AddrBits(11), .Bits(8)) ramdualaccess_3 (
    .str(STRHI), .C(clk), .ld(1'b1), .A1({Addr[9:0], Addr[11]}), .Din1(Data[7:0]),
    .A2({counter_1_out[11], B, C, D, counter_1_out_2[0], counter_1_out[5:0]}),
    .D2({ramdualaccess_3_d2_2, ramdualaccess_3_d2}));  // open: D1
  RAMDualAccess #(.AddrBits(11), .Bits(8)) ramdualaccess_4 (
    .str(STRHI), .C(clk), .ld(1'b1), .A1({Addr[9:0], Addr[11]}), .Din1({1'b0, Data[14:8]}),
    .A2({counter_1_out[11], B, C, D, counter_1_out_2[0], counter_1_out[5:0]}),
    .D2({ramdualaccess_4_d2_2[7], ramdualaccess_4_d2}));  // open: D1
  Demultiplexer demultiplexer_2 (.sel(counter_1_out[11]), .in(clk), .out_0(CLK3), .out_1(CLK4));
  EEPROM #(.AddrBits(15), .Bits(8)) eeprom_1 (
    .A({A, B, C, D, counter_1_out_2[0], ramdualaccess_3_d2, ramdualaccess_1_d2}), .CS(1'b1), .WE(1'b0),
    .OE(1'b1), .D({eeprom_1_d, R2, R1}));
  EEPROM #(.AddrBits(15), .Bits(8)) eeprom_2 (
    .A({A, B, C, D, counter_1_out_2[0], ramdualaccess_4_d2[1:0], ramdualaccess_3_d2_2, ramdualaccess_2_d2[1:0], ramdualaccess_1_d2_2}),
    .CS(1'b1), .WE(1'b0), .OE(1'b1), .D({eeprom_2_d, G2, G1}));
  EEPROM #(.AddrBits(15), .Bits(8)) eeprom_3 (
    .A({A, B, C, D, counter_1_out_2[0], ramdualaccess_4_d2[6:2], ramdualaccess_2_d2[6:2]}), .CS(1'b1),
    .WE(1'b0), .OE(1'b1), .D({eeprom_3_d, B2, B1}));

  assign OE = 1'b1;

  // Other names for the same wires on the sheet: ADDRIN[10:0] = {Addr[9:0], Addr[11]}

  // Notes on the sheet:
  //   contents of eeprom_1 (hex, n*v repeats v):
  //   0,31*1,2,31*3,2,31*3,2,31*3,2,31*3,2,31*3,2,31*3,2,31*3,2,31*3
  //   ,2,31*3,2,31*3,2,31*3,2,31*3,2,31*3,2,31*3,2,31*3,2,31*3,2,31*3
  //   ,2,31*3,2,31*3,2,31*3,2,31*3,2,31*3,2,31*3,2,31*3,2,31*3,2,31*3
  //   ,2,31*3,2,31*3,2,31*3,2,31*3,2,31*3,0,0,30*1,0,0,30*1,2,2,30*3
  //   ,2,2,30*3,2,2,30*3,2,2,30*3,2,2,30*3,2,2,30*3,2,2,30*3,2,2,30*3
  //   ,2,2,30*3,2,2,30*3,2,2,30*3,2,2,30*3,2,2,30*3,2,2,30*3,2,2,30*3
  //   ,2,2,30*3,2,2,30*3,2,2,30*3,2,2,30*3,2,2,30*3,2,2,30*3,2,2,30*3
  //   ,2,2,30*3,2,2,30*3,2,2,30*3,2,2,30*3,2,2,30*3,2,2,30*3,2,2,30*3
  //   ,2,2,30*3,0,0,0,29*1,0,0,0,29*1,0,0,0,29*1,2,2,2,29*3,2,2,2,29*3
  //   ,2,2,2,29*3,2,2,2,29*3,2,2,2,29*3,2,2,2,29*3,2,2,2,29*3,2,2,2
  //   ,29*3,2,2,2,29*3,2,2,2,29*3,2,2,2,29*3,2,2,2,29*3,2,2,2,29*3,2,2,2
  //   ,29*3,2,2,2,29*3,2,2,2,29*3,2,2,2,29*3,2,2,2,29*3,2,2,2,29*3,2,2,2
  //   ,29*3,2,2,2,29*3,2,2,2,29*3,2,2,2,29*3,2,2,2,29*3,2,2,2,29*3,2,2,2
  //   ,29*3,2,2,2,29*3,2,2,2,29*3,2,2,2,29*3,4*0,28*1,4*0,28*1,4*0,28*1
  //   ,4*0,28*1,4*2,28*3,4*2,28*3,4*2,28*3,4*2,28*3,4*2,28*3,4*2,28*3
  //   ,4*2,28*3,4*2,28*3,4*2,28*3,4*2,28*3,4*2,28*3,4*2,28*3,4*2,28*3
  //   ,4*2,28*3,4*2,28*3,4*2,28*3,4*2,28*3,4*2,28*3,4*2,28*3,4*2,28*3
  //   ,4*2,28*3,4*2,28*3,4*2,28*3,4*2,28*3,4*2,28*3,4*2,28*3,4*2,28*3
  //   ,4*2,28*3,5*0,27*1,5*0,27*1,5*0,27*1,5*0,27*1,5*0,27*1,5*2,27*3
  //   ,5*2,27*3,5*2,27*3,5*2,27*3,5*2,27*3,5*2,27*3,5*2,27*3,5*2,27*3
  //   ,5*2,27*3,5*2,27*3,5*2,27*3,5*2,27*3,5*2,27*3,5*2,27*3,5*2,27*3
  //   ,5*2,27*3,5*2,27*3,5*2,27*3,5*2,27*3,5*2,27*3,5*2,27*3,5*2,27*3
  //   ,5*2,27*3,5*2,27*3,5*2,27*3,5*2,27*3,5*2,27*3,6*0,26*1,6*0,26*1
  //   ,6*0,26*1,6*0,26*1,6*0,26*1,6*0,26*1,6*2,26*3,6*2,26*3,6*2,26*3
  //   ,6*2,26*3,6*2,26*3,6*2,26*3,6*2,26*3,6*2,26*3,6*2,26*3,6*2,26*3
  //   ,6*2,26*3,6*2,26*3,6*2,26*3,6*2,26*3,6*2,26*3,6*2,26*3,6*2,26*3
  //   ,6*2,26*3,6*2,26*3,6*2,26*3,6*2,26*3,6*2,26*3,6*2,26*3,6*2,26*3
  //   ,6*2,26*3,6*2,26*3,7*0,25*1,7*0,25*1,7*0,25*1,7*0,25*1,7*0,25*1
  //   ,7*0,25*1,7*0,25*1,7*2,25*3,7*2,25*3,7*2,25*3,7*2,25*3,7*2,25*3
  //   ,7*2,25*3,7*2,25*3,7*2,25*3,7*2,25*3,7*2,25*3,7*2,25*3,7*2,25*3
  //   ,7*2,25*3,7*2,25*3,7*2,25*3,7*2,25*3,7*2,25*3,7*2,25*3,7*2,25*3
  //   ,7*2,25*3,7*2,25*3,7*2,25*3,7*2,25*3,7*2,25*3,7*2,25*3,8*0,24*1
  //   ,8*0,24*1,8*0,24*1,8*0,24*1,8*0,24*1,8*0,24*1,8*0,24*1,8*0,24*1
  //   ,8*2,24*3,8*2,24*3,8*2,24*3,8*2,24*3,8*2,24*3,8*2,24*3,8*2,24*3
  //   ,8*2,24*3,8*2,24*3,8*2,24*3,8*2,24*3,8*2,24*3,8*2,24*3,8*2,24*3
  //   ,8*2,24*3,8*2,24*3,8*2,24*3,8*2,24*3,8*2,24*3,8*2,24*3,8*2,24*3
  //   ,8*2,24*3,8*2,24*3,8*2,24*3,9*0,23*1,9*0,23*1,9*0,23*1,9*0,23*1
  //   ,9*0,23*1,9*0,23*1,9*0,23*1,9*0,23*1,9*0,23*1,9*2,23*3,9*2,23*3
  //   ,9*2,23*3,9*2,23*3,9*2,23*3,9*2,23*3,9*2,23*3,9*2,23*3,9*2,23*3
  //   ,9*2,23*3,9*2,23*3,9*2,23*3,9*2,23*3,9*2,23*3,9*2,23*3,9*2,23*3
  //   ,9*2,23*3,9*2,23*3,9*2,23*3,9*2,23*3,9*2,23*3,9*2,23*3,9*2,23*3
  //   ,10*0,22*1,10*0,22*1,10*0,22*1,10*0,22*1,10*0,22*1,10*0,22*1,10*0
  //   ,22*1,10*0,22*1,10*0,22*1,10*0,22*1,10*2,22*3,10*2,22*3,10*2,22*3
  //   ,10*2,22*3,10*2,22*3,10*2,22*3,10*2,22*3,10*2,22*3,10*2,22*3,10*2
  //   ,22*3,10*2,22*3,10*2,22*3,10*2,22*3,10*2,22*3,10*2,22*3,10*2,22*3
  //   ,10*2,22*3,10*2,22*3,10*2,22*3,10*2,22*3,10*2,22*3,10*2,22*3,11*0
  //   ,21*1,11*0,21*1,11*0,21*1,11*0,21*1,11*0,21*1,11*0,21*1,11*0,21*1
  //   ,11*0,21*1,11*0,21*1,11*0,21*1,11*0,21*1,11*2,21*3,11*2,21*3,11*2
  //   ,21*3,11*2,21*3,11*2,21*3,11*2,21*3,11*2,21*3,11*2,21*3,11*2,21*3
  //   ,11*2,21*3,11*2,21*3,11*2,21*3,11*2,21*3,11*2,21*3,11*2,21*3,11*2
  //   ,21*3,11*2,21*3,11*2,21*3,11*2,21*3,11*2,21*3,11*2,21*3,12*0,20*1
  //   ,12*0,20*1,12*0,20*1,12*0,20*1,12*0,20*1,12*0,20*1,12*0,20*1,12*0
  //   ,20*1,12*0,20*1,12*0,20*1,12*0,20*1,12*0,20*1,12*2,20*3,12*2,20*3
  //   ,12*2,20*3,12*2,20*3,12*2,20*3,12*2,20*3,12*2,20*3,12*2,20*3,12*2
  //   ,20*3,12*2,20*3,12*2,20*3,12*2,20*3,12*2,20*3,12*2,20*3,12*2,20*3
  //   ,12*2,20*3,12*2,20*3,12*2,20*3,12*2,20*3,12*2,20*3,13*0,19*1,13*0
  //   ,19*1,13*0,19*1,13*0,19*1,13*0,19*1,13*0,19*1,13*0,19*1,13*0,19*1
  //   ,13*0,19*1,13*0,19*1,13*0,19*1,13*0,19*1,13*0,19*1,13*2,19*3,13*2
  //   ,19*3,13*2,19*3,13*2,19*3,13*2,19*3,13*2,19*3,13*2,19*3,13*2,19*3
  //   ,13*2,19*3,13*2,19*3,13*2,19*3,13*2,19*3,13*2,19*3,13*2,19*3,13*2
  //   ,19*3,13*2,19*3,13*2,19*3,13*2,19*3,13*2,19*3,14*0,18*1,14*0,18*1
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  //   contents of eeprom_2 (hex, n*v repeats v):
  //   0,31*1,2,31*3,2,31*3,2,31*3,2,31*3,2,31*3,2,31*3,2,31*3,2,31*3
  //   ,2,31*3,2,31*3,2,31*3,2,31*3,2,31*3,2,31*3,2,31*3,2,31*3,2,31*3
  //   ,2,31*3,2,31*3,2,31*3,2,31*3,2,31*3,2,31*3,2,31*3,2,31*3,2,31*3
  //   ,2,31*3,2,31*3,2,31*3,2,31*3,2,31*3,0,0,30*1,0,0,30*1,2,2,30*3
  //   ,2,2,30*3,2,2,30*3,2,2,30*3,2,2,30*3,2,2,30*3,2,2,30*3,2,2,30*3
  //   ,2,2,30*3,2,2,30*3,2,2,30*3,2,2,30*3,2,2,30*3,2,2,30*3,2,2,30*3
  //   ,2,2,30*3,2,2,30*3,2,2,30*3,2,2,30*3,2,2,30*3,2,2,30*3,2,2,30*3
  //   ,2,2,30*3,2,2,30*3,2,2,30*3,2,2,30*3,2,2,30*3,2,2,30*3,2,2,30*3
  //   ,2,2,30*3,0,0,0,29*1,0,0,0,29*1,0,0,0,29*1,2,2,2,29*3,2,2,2,29*3
  //   ,2,2,2,29*3,2,2,2,29*3,2,2,2,29*3,2,2,2,29*3,2,2,2,29*3,2,2,2
  //   ,29*3,2,2,2,29*3,2,2,2,29*3,2,2,2,29*3,2,2,2,29*3,2,2,2,29*3,2,2,2
  //   ,29*3,2,2,2,29*3,2,2,2,29*3,2,2,2,29*3,2,2,2,29*3,2,2,2,29*3,2,2,2
  //   ,29*3,2,2,2,29*3,2,2,2,29*3,2,2,2,29*3,2,2,2,29*3,2,2,2,29*3,2,2,2
  //   ,29*3,2,2,2,29*3,2,2,2,29*3,2,2,2,29*3,4*0,28*1,4*0,28*1,4*0,28*1
  //   ,4*0,28*1,4*2,28*3,4*2,28*3,4*2,28*3,4*2,28*3,4*2,28*3,4*2,28*3
  //   ,4*2,28*3,4*2,28*3,4*2,28*3,4*2,28*3,4*2,28*3,4*2,28*3,4*2,28*3
  //   ,4*2,28*3,4*2,28*3,4*2,28*3,4*2,28*3,4*2,28*3,4*2,28*3,4*2,28*3
  //   ,4*2,28*3,4*2,28*3,4*2,28*3,4*2,28*3,4*2,28*3,4*2,28*3,4*2,28*3
  //   ,4*2,28*3,5*0,27*1,5*0,27*1,5*0,27*1,5*0,27*1,5*0,27*1,5*2,27*3
  //   ,5*2,27*3,5*2,27*3,5*2,27*3,5*2,27*3,5*2,27*3,5*2,27*3,5*2,27*3
  //   ,5*2,27*3,5*2,27*3,5*2,27*3,5*2,27*3,5*2,27*3,5*2,27*3,5*2,27*3
  //   ,5*2,27*3,5*2,27*3,5*2,27*3,5*2,27*3,5*2,27*3,5*2,27*3,5*2,27*3
  //   ,5*2,27*3,5*2,27*3,5*2,27*3,5*2,27*3,5*2,27*3,6*0,26*1,6*0,26*1
  //   ,6*0,26*1,6*0,26*1,6*0,26*1,6*0,26*1,6*2,26*3,6*2,26*3,6*2,26*3
  //   ,6*2,26*3,6*2,26*3,6*2,26*3,6*2,26*3,6*2,26*3,6*2,26*3,6*2,26*3
  //   ,6*2,26*3,6*2,26*3,6*2,26*3,6*2,26*3,6*2,26*3,6*2,26*3,6*2,26*3
  //   ,6*2,26*3,6*2,26*3,6*2,26*3,6*2,26*3,6*2,26*3,6*2,26*3,6*2,26*3
  //   ,6*2,26*3,6*2,26*3,7*0,25*1,7*0,25*1,7*0,25*1,7*0,25*1,7*0,25*1
  //   ,7*0,25*1,7*0,25*1,7*2,25*3,7*2,25*3,7*2,25*3,7*2,25*3,7*2,25*3
  //   ,7*2,25*3,7*2,25*3,7*2,25*3,7*2,25*3,7*2,25*3,7*2,25*3,7*2,25*3
  //   ,7*2,25*3,7*2,25*3,7*2,25*3,7*2,25*3,7*2,25*3,7*2,25*3,7*2,25*3
  //   ,7*2,25*3,7*2,25*3,7*2,25*3,7*2,25*3,7*2,25*3,7*2,25*3,8*0,24*1
  //   ,8*0,24*1,8*0,24*1,8*0,24*1,8*0,24*1,8*0,24*1,8*0,24*1,8*0,24*1
  //   ,8*2,24*3,8*2,24*3,8*2,24*3,8*2,24*3,8*2,24*3,8*2,24*3,8*2,24*3
  //   ,8*2,24*3,8*2,24*3,8*2,24*3,8*2,24*3,8*2,24*3,8*2,24*3,8*2,24*3
  //   ,8*2,24*3,8*2,24*3,8*2,24*3,8*2,24*3,8*2,24*3,8*2,24*3,8*2,24*3
  //   ,8*2,24*3,8*2,24*3,8*2,24*3,9*0,23*1,9*0,23*1,9*0,23*1,9*0,23*1
  //   ,9*0,23*1,9*0,23*1,9*0,23*1,9*0,23*1,9*0,23*1,9*2,23*3,9*2,23*3
  //   ,9*2,23*3,9*2,23*3,9*2,23*3,9*2,23*3,9*2,23*3,9*2,23*3,9*2,23*3
  //   ,9*2,23*3,9*2,23*3,9*2,23*3,9*2,23*3,9*2,23*3,9*2,23*3,9*2,23*3
  //   ,9*2,23*3,9*2,23*3,9*2,23*3,9*2,23*3,9*2,23*3,9*2,23*3,9*2,23*3
  //   ,10*0,22*1,10*0,22*1,10*0,22*1,10*0,22*1,10*0,22*1,10*0,22*1,10*0
  //   ,22*1,10*0,22*1,10*0,22*1,10*0,22*1,10*2,22*3,10*2,22*3,10*2,22*3
  //   ,10*2,22*3,10*2,22*3,10*2,22*3,10*2,22*3,10*2,22*3,10*2,22*3,10*2
  //   ,22*3,10*2,22*3,10*2,22*3,10*2,22*3,10*2,22*3,10*2,22*3,10*2,22*3
  //   ,10*2,22*3,10*2,22*3,10*2,22*3,10*2,22*3,10*2,22*3,10*2,22*3,11*0
  //   ,21*1,11*0,21*1,11*0,21*1,11*0,21*1,11*0,21*1,11*0,21*1,11*0,21*1
  //   ,11*0,21*1,11*0,21*1,11*0,21*1,11*0,21*1,11*2,21*3,11*2,21*3,11*2
  //   ,21*3,11*2,21*3,11*2,21*3,11*2,21*3,11*2,21*3,11*2,21*3,11*2,21*3
  //   ,11*2,21*3,11*2,21*3,11*2,21*3,11*2,21*3,11*2,21*3,11*2,21*3,11*2
  //   ,21*3,11*2,21*3,11*2,21*3,11*2,21*3,11*2,21*3,11*2,21*3,12*0,20*1
  //   ,12*0,20*1,12*0,20*1,12*0,20*1,12*0,20*1,12*0,20*1,12*0,20*1,12*0
  //   ,20*1,12*0,20*1,12*0,20*1,12*0,20*1,12*0,20*1,12*2,20*3,12*2,20*3
  //   ,12*2,20*3,12*2,20*3,12*2,20*3,12*2,20*3,12*2,20*3,12*2,20*3,12*2
  //   ,20*3,12*2,20*3,12*2,20*3,12*2,20*3,12*2,20*3,12*2,20*3,12*2,20*3
  //   ,12*2,20*3,12*2,20*3,12*2,20*3,12*2,20*3,12*2,20*3,13*0,19*1,13*0
  //   ,19*1,13*0,19*1,13*0,19*1,13*0,19*1,13*0,19*1,13*0,19*1,13*0,19*1
  //   ,13*0,19*1,13*0,19*1,13*0,19*1,13*0,19*1,13*0,19*1,13*2,19*3,13*2
  //   ,19*3,13*2,19*3,13*2,19*3,13*2,19*3,13*2,19*3,13*2,19*3,13*2,19*3
  //   ,13*2,19*3,13*2,19*3,13*2,19*3,13*2,19*3,13*2,19*3,13*2,19*3,13*2
  //   ,19*3,13*2,19*3,13*2,19*3,13*2,19*3,13*2,19*3,14*0,18*1,14*0,18*1
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  //   contents of eeprom_3 (hex, n*v repeats v):
  //   0,31*1,2,31*3,2,31*3,2,31*3,2,31*3,2,31*3,2,31*3,2,31*3,2,31*3
  //   ,2,31*3,2,31*3,2,31*3,2,31*3,2,31*3,2,31*3,2,31*3,2,31*3,2,31*3
  //   ,2,31*3,2,31*3,2,31*3,2,31*3,2,31*3,2,31*3,2,31*3,2,31*3,2,31*3
  //   ,2,31*3,2,31*3,2,31*3,2,31*3,2,31*3,0,0,30*1,0,0,30*1,2,2,30*3
  //   ,2,2,30*3,2,2,30*3,2,2,30*3,2,2,30*3,2,2,30*3,2,2,30*3,2,2,30*3
  //   ,2,2,30*3,2,2,30*3,2,2,30*3,2,2,30*3,2,2,30*3,2,2,30*3,2,2,30*3
  //   ,2,2,30*3,2,2,30*3,2,2,30*3,2,2,30*3,2,2,30*3,2,2,30*3,2,2,30*3
  //   ,2,2,30*3,2,2,30*3,2,2,30*3,2,2,30*3,2,2,30*3,2,2,30*3,2,2,30*3
  //   ,2,2,30*3,0,0,0,29*1,0,0,0,29*1,0,0,0,29*1,2,2,2,29*3,2,2,2,29*3
  //   ,2,2,2,29*3,2,2,2,29*3,2,2,2,29*3,2,2,2,29*3,2,2,2,29*3,2,2,2
  //   ,29*3,2,2,2,29*3,2,2,2,29*3,2,2,2,29*3,2,2,2,29*3,2,2,2,29*3,2,2,2
  //   ,29*3,2,2,2,29*3,2,2,2,29*3,2,2,2,29*3,2,2,2,29*3,2,2,2,29*3,2,2,2
  //   ,29*3,2,2,2,29*3,2,2,2,29*3,2,2,2,29*3,2,2,2,29*3,2,2,2,29*3,2,2,2
  //   ,29*3,2,2,2,29*3,2,2,2,29*3,2,2,2,29*3,4*0,28*1,4*0,28*1,4*0,28*1
  //   ,4*0,28*1,4*2,28*3,4*2,28*3,4*2,28*3,4*2,28*3,4*2,28*3,4*2,28*3
  //   ,4*2,28*3,4*2,28*3,4*2,28*3,4*2,28*3,4*2,28*3,4*2,28*3,4*2,28*3
  //   ,4*2,28*3,4*2,28*3,4*2,28*3,4*2,28*3,4*2,28*3,4*2,28*3,4*2,28*3
  //   ,4*2,28*3,4*2,28*3,4*2,28*3,4*2,28*3,4*2,28*3,4*2,28*3,4*2,28*3
  //   ,4*2,28*3,5*0,27*1,5*0,27*1,5*0,27*1,5*0,27*1,5*0,27*1,5*2,27*3
  //   ,5*2,27*3,5*2,27*3,5*2,27*3,5*2,27*3,5*2,27*3,5*2,27*3,5*2,27*3
  //   ,5*2,27*3,5*2,27*3,5*2,27*3,5*2,27*3,5*2,27*3,5*2,27*3,5*2,27*3
  //   ,5*2,27*3,5*2,27*3,5*2,27*3,5*2,27*3,5*2,27*3,5*2,27*3,5*2,27*3
  //   ,5*2,27*3,5*2,27*3,5*2,27*3,5*2,27*3,5*2,27*3,6*0,26*1,6*0,26*1
  //   ,6*0,26*1,6*0,26*1,6*0,26*1,6*0,26*1,6*2,26*3,6*2,26*3,6*2,26*3
  //   ,6*2,26*3,6*2,26*3,6*2,26*3,6*2,26*3,6*2,26*3,6*2,26*3,6*2,26*3
  //   ,6*2,26*3,6*2,26*3,6*2,26*3,6*2,26*3,6*2,26*3,6*2,26*3,6*2,26*3
  //   ,6*2,26*3,6*2,26*3,6*2,26*3,6*2,26*3,6*2,26*3,6*2,26*3,6*2,26*3
  //   ,6*2,26*3,6*2,26*3,7*0,25*1,7*0,25*1,7*0,25*1,7*0,25*1,7*0,25*1
  //   ,7*0,25*1,7*0,25*1,7*2,25*3,7*2,25*3,7*2,25*3,7*2,25*3,7*2,25*3
  //   ,7*2,25*3,7*2,25*3,7*2,25*3,7*2,25*3,7*2,25*3,7*2,25*3,7*2,25*3
  //   ,7*2,25*3,7*2,25*3,7*2,25*3,7*2,25*3,7*2,25*3,7*2,25*3,7*2,25*3
  //   ,7*2,25*3,7*2,25*3,7*2,25*3,7*2,25*3,7*2,25*3,7*2,25*3,8*0,24*1
  //   ,8*0,24*1,8*0,24*1,8*0,24*1,8*0,24*1,8*0,24*1,8*0,24*1,8*0,24*1
  //   ,8*2,24*3,8*2,24*3,8*2,24*3,8*2,24*3,8*2,24*3,8*2,24*3,8*2,24*3
  //   ,8*2,24*3,8*2,24*3,8*2,24*3,8*2,24*3,8*2,24*3,8*2,24*3,8*2,24*3
  //   ,8*2,24*3,8*2,24*3,8*2,24*3,8*2,24*3,8*2,24*3,8*2,24*3,8*2,24*3
  //   ,8*2,24*3,8*2,24*3,8*2,24*3,9*0,23*1,9*0,23*1,9*0,23*1,9*0,23*1
  //   ,9*0,23*1,9*0,23*1,9*0,23*1,9*0,23*1,9*0,23*1,9*2,23*3,9*2,23*3
  //   ,9*2,23*3,9*2,23*3,9*2,23*3,9*2,23*3,9*2,23*3,9*2,23*3,9*2,23*3
  //   ,9*2,23*3,9*2,23*3,9*2,23*3,9*2,23*3,9*2,23*3,9*2,23*3,9*2,23*3
  //   ,9*2,23*3,9*2,23*3,9*2,23*3,9*2,23*3,9*2,23*3,9*2,23*3,9*2,23*3
  //   ,10*0,22*1,10*0,22*1,10*0,22*1,10*0,22*1,10*0,22*1,10*0,22*1,10*0
  //   ,22*1,10*0,22*1,10*0,22*1,10*0,22*1,10*2,22*3,10*2,22*3,10*2,22*3
  //   ,10*2,22*3,10*2,22*3,10*2,22*3,10*2,22*3,10*2,22*3,10*2,22*3,10*2
  //   ,22*3,10*2,22*3,10*2,22*3,10*2,22*3,10*2,22*3,10*2,22*3,10*2,22*3
  //   ,10*2,22*3,10*2,22*3,10*2,22*3,10*2,22*3,10*2,22*3,10*2,22*3,11*0
  //   ,21*1,11*0,21*1,11*0,21*1,11*0,21*1,11*0,21*1,11*0,21*1,11*0,21*1
  //   ,11*0,21*1,11*0,21*1,11*0,21*1,11*0,21*1,11*2,21*3,11*2,21*3,11*2
  //   ,21*3,11*2,21*3,11*2,21*3,11*2,21*3,11*2,21*3,11*2,21*3,11*2,21*3
  //   ,11*2,21*3,11*2,21*3,11*2,21*3,11*2,21*3,11*2,21*3,11*2,21*3,11*2
  //   ,21*3,11*2,21*3,11*2,21*3,11*2,21*3,11*2,21*3,11*2,21*3,12*0,20*1
  //   ,12*0,20*1,12*0,20*1,12*0,20*1,12*0,20*1,12*0,20*1,12*0,20*1,12*0
  //   ,20*1,12*0,20*1,12*0,20*1,12*0,20*1,12*0,20*1,12*2,20*3,12*2,20*3
  //   ,12*2,20*3,12*2,20*3,12*2,20*3,12*2,20*3,12*2,20*3,12*2,20*3,12*2
  //   ,20*3,12*2,20*3,12*2,20*3,12*2,20*3,12*2,20*3,12*2,20*3,12*2,20*3
  //   ,12*2,20*3,12*2,20*3,12*2,20*3,12*2,20*3,12*2,20*3,13*0,19*1,13*0
  //   ,19*1,13*0,19*1,13*0,19*1,13*0,19*1,13*0,19*1,13*0,19*1,13*0,19*1
  //   ,13*0,19*1,13*0,19*1,13*0,19*1,13*0,19*1,13*0,19*1,13*2,19*3,13*2
  //   ,19*3,13*2,19*3,13*2,19*3,13*2,19*3,13*2,19*3,13*2,19*3,13*2,19*3
  //   ,13*2,19*3,13*2,19*3,13*2,19*3,13*2,19*3,13*2,19*3,13*2,19*3,13*2
  //   ,19*3,13*2,19*3,13*2,19*3,13*2,19*3,13*2,19*3,14*0,18*1,14*0,18*1
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endmodule
