// Digital circuit SevenSegment.dig as structural Verilog
module SevenSegment (
  input  clk,
  input  [15:0] IN
);

  wire demultiplexer_1_out_0, demultiplexer_1_out_1, demultiplexer_1_out_2, demultiplexer_1_out_3, not_1_out,
       not_2_out, not_3_out, not_4_out;
  wire [1:0] counter_1_out;
  wire [7:0] eeprom_1_d;

  Counter #(.Bits(2)) counter_1 (.en(1'b1), .C(clk), .clr(1'b0), .out(counter_1_out));  // open: ovf
  EEPROM #(.AddrBits(18), .Bits(8)) eeprom_1 (.A({counter_1_out, IN}), .CS(1'b1), .WE(1'b0), .OE(1'b1), .D(eeprom_1_d));
  Demultiplexer #(.Selector_Bits(2)) demultiplexer_1 (
    .sel(counter_1_out), .in(1'b1), .out_0(demultiplexer_1_out_0), .out_1(demultiplexer_1_out_1),
    .out_2(demultiplexer_1_out_2), .out_3(demultiplexer_1_out_3));
  not not_1 (not_1_out, demultiplexer_1_out_0);
  not not_2 (not_2_out, demultiplexer_1_out_1);
  not not_3 (not_3_out, demultiplexer_1_out_2);
  not not_4 (not_4_out, demultiplexer_1_out_3);
  Seven_Seg #(.commonCathode("true"), .persistTime(14)) seven_seg_1 (
    .a(eeprom_1_d[0]), .b(eeprom_1_d[1]), .c(eeprom_1_d[2]), .d(eeprom_1_d[3]), .e(eeprom_1_d[4]),
    .f(eeprom_1_d[5]), .g(eeprom_1_d[6]), .dp(1'b0), .common(not_4_out));
  Seven_Seg #(.commonCathode("true"), .persistTime(14)) seven_seg_2 (
    .a(eeprom_1_d[0]), .b(eeprom_1_d[1]), .c(eeprom_1_d[2]), .d(eeprom_1_d[3]), .e(eeprom_1_d[4]),
    .f(eeprom_1_d[5]), .g(eeprom_1_d[6]), .dp(1'b0), .common(not_3_out));
  Seven_Seg #(.commonCathode("true"), .persistTime(14)) seven_seg_3 (
    .a(eeprom_1_d[0]), .b(eeprom_1_d[1]), .c(eeprom_1_d[2]), .d(eeprom_1_d[3]), .e(eeprom_1_d[4]),
    .f(eeprom_1_d[5]), .g(eeprom_1_d[6]), .dp(1'b0), .common(not_2_out));
  Seven_Seg #(.commonCathode("true"), .persistTime(14)) seven_seg_4 (
    .a(eeprom_1_d[0]), .b(eeprom_1_d[1]), .c(eeprom_1_d[2]), .d(eeprom_1_d[3]), .e(eeprom_1_d[4]),
    .f(eeprom_1_d[5]), .g(eeprom_1_d[6]), .dp(1'b0), .common(not_1_out));

  // Notes on the sheet:
  //   clk: Hz: 2147483647
  //   contents of eeprom_1 (hex, n*v repeats v):
  //   3f,6,5b,4f,66,6d,7d,7,7f,6f,77,7c,39,5e,79,71,3f,6,5b,4f,66,6d
  //   ,7d,7,7f,6f,77,7c,39,5e,79,71,3f,6,5b,4f,66,6d,7d,7,7f,6f,77,7c
  //   ,39,5e,79,71,3f,6,5b,4f,66,6d,7d,7,7f,6f,77,7c,39,5e,79,71,3f
  //   ,6,5b,4f,66,6d,7d,7,7f,6f,77,7c,39,5e,79,71,3f,6,5b,4f,66,6d,7d
  //   ,7,7f,6f,77,7c,39,5e,79,71,3f,6,5b,4f,66,6d,7d,7,7f,6f,77,7c,39
  //   ,5e,79,71,3f,6,5b,4f,66,6d,7d,7,7f,6f,77,7c,39,5e,79,71,3f,6,5b
  //   ,4f,66,6d,7d,7,7f,6f,77,7c,39,5e,79,71,3f,6,5b,4f,66,6d,7d,7,7f
  //   ,6f,77,7c,39,5e,79,71,3f,6,5b,4f,66,6d,7d,7,7f,6f,77,7c,39,5e
  //   ,79,71,3f,6,5b,4f,66,6d,7d,7,7f,6f,77,7c,39,5e,79,71,3f,6,5b,4f
  //   ,66,6d,7d,7,7f,6f,77,7c,39,5e,79,71,3f,6,5b,4f,66,6d,7d,7,7f,6f
  //   ,77,7c,39,5e,79,71,3f,6,5b,4f,66,6d,7d,7,7f,6f,77,7c,39,5e,79
  //   ,71,3f,6,5b,4f,66,6d,7d,7,7f,6f,77,7c,39,5e,79,71,3f,6,5b,4f,66
  //   ,6d,7d,7,7f,6f,77,7c,39,5e,79,71,3f,6,5b,4f,66,6d,7d,7,7f,6f,77
  //   ,7c,39,5e,79,71,3f,6,5b,4f,66,6d,7d,7,7f,6f,77,7c,39,5e,79,71
  //   ,3f,6,5b,4f,66,6d,7d,7,7f,6f,77,7c,39,5e,79,71,3f,6,5b,4f,66,6d
  //   ,7d,7,7f,6f,77,7c,39,5e,79,71,3f,6,5b,4f,66,6d,7d,7,7f,6f,77,7c
  //   ,39,5e,79,71,3f,6,5b,4f,66,6d,7d,7,7f,6f,77,7c,39,5e,79,71,3f
  //   ,6,5b,4f,66,6d,7d,7,7f,6f,77,7c,39,5e,79,71,3f,6,5b,4f,66,6d,7d
  //   ,7,7f,6f,77,7c,39,5e,79,71,3f,6,5b,4f,66,6d,7d,7,7f,6f,77,7c,39
  //   ,5e,79,71,3f,6,5b,4f,66,6d,7d,7,7f,6f,77,7c,39,5e,79,71,3f,6,5b
  //   ,4f,66,6d,7d,7,7f,6f,77,7c,39,5e,79,71,3f,6,5b,4f,66,6d,7d,7,7f
  //   ,6f,77,7c,39,5e,79,71,3f,6,5b,4f,66,6d,7d,7,7f,6f,77,7c,39,5e
  //   ,79,71,3f,6,5b,4f,66,6d,7d,7,7f,6f,77,7c,39,5e,79,71,3f,6,5b,4f
  //   ,66,6d,7d,7,7f,6f,77,7c,39,5e,79,71,3f,6,5b,4f,66,6d,7d,7,7f,6f
  //   ,77,7c,39,5e,79,71,3f,6,5b,4f,66,6d,7d,7,7f,6f,77,7c,39,5e,79
  //   ,71,3f,6,5b,4f,66,6d,7d,7,7f,6f,77,7c,39,5e,79,71,3f,6,5b,4f,66
  //   ,6d,7d,7,7f,6f,77,7c,39,5e,79,71,3f,6,5b,4f,66,6d,7d,7,7f,6f,77
  //   ,7c,39,5e,79,71,3f,6,5b,4f,66,6d,7d,7,7f,6f,77,7c,39,5e,79,71
  //   ,3f,6,5b,4f,66,6d,7d,7,7f,6f,77,7c,39,5e,79,71,3f,6,5b,4f,66,6d
  //   ,7d,7,7f,6f,77,7c,39,5e,79,71,3f,6,5b,4f,66,6d,7d,7,7f,6f,77,7c
  //   ,39,5e,79,71,3f,6,5b,4f,66,6d,7d,7,7f,6f,77,7c,39,5e,79,71,3f
  //   ,6,5b,4f,66,6d,7d,7,7f,6f,77,7c,39,5e,79,71,3f,6,5b,4f,66,6d,7d
  //   ,7,7f,6f,77,7c,39,5e,79,71,3f,6,5b,4f,66,6d,7d,7,7f,6f,77,7c,39
  //   ,5e,79,71,3f,6,5b,4f,66,6d,7d,7,7f,6f,77,7c,39,5e,79,71,3f,6,5b
  //   ,4f,66,6d,7d,7,7f,6f,77,7c,39,5e,79,71,3f,6,5b,4f,66,6d,7d,7,7f
  //   ,6f,77,7c,39,5e,79,71,3f,6,5b,4f,66,6d,7d,7,7f,6f,77,7c,39,5e
  //   ,79,71,3f,6,5b,4f,66,6d,7d,7,7f,6f,77,7c,39,5e,79,71,3f,6,5b,4f
  //   ,66,6d,7d,7,7f,6f,77,7c,39,5e,79,71,3f,6,5b,4f,66,6d,7d,7,7f,6f
  //   ,77,7c,39,5e,79,71,3f,6,5b,4f,66,6d,7d,7,7f,6f,77,7c,39,5e,79
  //   ,71,3f,6,5b,4f,66,6d,7d,7,7f,6f,77,7c,39,5e,79,71,3f,6,5b,4f,66
  //   ,6d,7d,7,7f,6f,77,7c,39,5e,79,71,3f,6,5b,4f,66,6d,7d,7,7f,6f,77
  //   ,7c,39,5e,79,71,3f,6,5b,4f,66,6d,7d,7,7f,6f,77,7c,39,5e,79,71
  //   ,3f,6,5b,4f,66,6d,7d,7,7f,6f,77,7c,39,5e,79,71,3f,6,5b,4f,66,6d
  //   ,7d,7,7f,6f,77,7c,39,5e,79,71,3f,6,5b,4f,66,6d,7d,7,7f,6f,77,7c
  //   ,39,5e,79,71,3f,6,5b,4f,66,6d,7d,7,7f,6f,77,7c,39,5e,79,71,3f
  //   ,6,5b,4f,66,6d,7d,7,7f,6f,77,7c,39,5e,79,71,3f,6,5b,4f,66,6d,7d
  //   ,7,7f,6f,77,7c,39,5e,79,71,3f,6,5b,4f,66,6d,7d,7,7f,6f,77,7c,39
  //   ,5e,79,71,3f,6,5b,4f,66,6d,7d,7,7f,6f,77,7c,39,5e,79,71,3f,6,5b
  //   ,4f,66,6d,7d,7,7f,6f,77,7c,39,5e,79,71,3f,6,5b,4f,66,6d,7d,7,7f
  //   ,6f,77,7c,39,5e,79,71,3f,6,5b,4f,66,6d,7d,7,7f,6f,77,7c,39,5e
  //   ,79,71,3f,6,5b,4f,66,6d,7d,7,7f,6f,77,7c,39,5e,79,71,3f,6,5b,4f
  //   ,66,6d,7d,7,7f,6f,77,7c,39,5e,79,71,3f,6,5b,4f,66,6d,7d,7,7f,6f
  //   ,77,7c,39,5e,79,71,3f,6,5b,4f,66,6d,7d,7,7f,6f,77,7c,39,5e,79
  //   ,71,3f,6,5b,4f,66,6d,7d,7,7f,6f,77,7c,39,5e,79,71,3f,6,5b,4f,66
  //   ,6d,7d,7,7f,6f,77,7c,39,5e,79,71,3f,6,5b,4f,66,6d,7d,7,7f,6f,77
  //   ,7c,39,5e,79,71,3f,6,5b,4f,66,6d,7d,7,7f,6f,77,7c,39,5e,79,71
  //   ,3f,6,5b,4f,66,6d,7d,7,7f,6f,77,7c,39,5e,79,71,3f,6,5b,4f,66,6d
  //   ,7d,7,7f,6f,77,7c,39,5e,79,71,3f,6,5b,4f,66,6d,7d,7,7f,6f,77,7c
  //   ,39,5e,79,71,3f,6,5b,4f,66,6d,7d,7,7f,6f,77,7c,39,5e,79,71,3f
  //   ,6,5b,4f,66,6d,7d,7,7f,6f,77,7c,39,5e,79,71,3f,6,5b,4f,66,6d,7d
  //   ,7,7f,6f,77,7c,39,5e,79,71,3f,6,5b,4f,66,6d,7d,7,7f,6f,77,7c,39
  //   ,5e,79,71,3f,6,5b,4f,66,6d,7d,7,7f,6f,77,7c,39,5e,79,71,3f,6,5b
  //   ,4f,66,6d,7d,7,7f,6f,77,7c,39,5e,79,71,3f,6,5b,4f,66,6d,7d,7,7f
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endmodule
